// Logisim project ha_solution.circ as structural Verilog: 1 circuit, main circuit half_adder
module half_adder (
  input  BIT1,
  input  BIT2,
  output COUT,
  output SUM
);

  Adder #(.width(1)) adder_1 (.a(BIT1), .b(BIT2), .out(COUT), .cout(SUM));  // open: cin
endmodule
