// Logisim project main.circ as structural Verilog: 1 circuit, main circuit main
module main (
  output SUM,
  output COUT,
  output [1:0] Input,
  output halt
);

  wire clock_1_out;
  wire [1:0] counter_1_q;

  Clock clock_1 (.out(clock_1_out));
  Counter #(.width(2), .max('h3)) counter_1 (
    .Q(counter_1_q), .carry(halt), .clk(clock_1_out));  // open: load, D, count, clr
  RAM #(.addrWidth(2), .dataWidth(2)) ram_1 (
    .addr(counter_1_q), .data(Input), .clk(clock_1_out));  // open: sel, ld, clr
  half_adder HA (.BIT1(Input[0]), .BIT2(Input[1]), .COUT(SUM), .SUM(COUT));
endmodule
