// Logisim project ha_query.circ as structural Verilog: 1 circuit, main circuit half_adder
// HA
module half_adder (
  input  BIT1,
  input  BIT2,
  output SUM,
  output COUT
);

  xor xor_1 (SUM, BIT1, BIT2);
  and and_1 (COUT, BIT1, BIT2);
endmodule
